# Fritzing sketch OutsideBathroomSchematic (saved by Fritzing 0.9.9b)
breadboards: 1

parts:
  OutsideBathroomSchematic = Particle Argon
  LED1 = LED - 3mm [color="Red (633nm)" current=0.030 package="3 mm [THT]"]
  LED2 = LED - 3mm [color="Blue (470nm)" current=0.030 package="3 mm [THT]"]
  R1 = Resistor [tolerance=±5% power=0.25 resistance=220 package=THT]
  R2 = Resistor [tolerance=±5% power=0.25 resistance=220 package=THT]
  WeMos_D1_Mini_OLED_Shield1 = WeMos D1 Mini OLED Shield

nets:
  3.3V: OutsideBathroomSchematic.3.3V, WeMos_D1_Mini_OLED_Shield1.3V3
  N1: OutsideBathroomSchematic.GND, WeMos_D1_Mini_OLED_Shield1.G
  N2: OutsideBathroomSchematic.SDA, WeMos_D1_Mini_OLED_Shield1.D3
  N3: OutsideBathroomSchematic.SCL, WeMos_D1_Mini_OLED_Shield1.D4
  N4: OutsideBathroomSchematic.D3, LED2.anode
  N5: OutsideBathroomSchematic.D4, LED1.anode
  N6: LED1.cathode, R1.Pin_0
  N7: LED2.cathode, R2.Pin_0
  N8: R1.Pin_1, R2.Pin_1

custom parts:
  Particle Argon: The Argon is a powerful Wi-Fi enabled development board that can act as either a standalone Wi-Fi endpoint or Wi-Fi enabled gateway for Particle Mesh networks. It is based on the Nordic nRF52840 and has built-in battery charging circuitry so it’s easy to connect a Li-Po and deploy your local network in minutes. The Argon is great for connecting existing projects to the Particle Device Cloud or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
