# Fritzing sketch InsideBathroomSchematic (saved by Fritzing 0.9.9b)
circuit board: 8.46667cm x 5.64444cm
breadboards: 1

parts:
  Argon1 = Particle Argon
  R1 = PHOTOCELL [package=photocell-kit]
  HC-SR04_Sensor_1 = HC-SR04 Ultrasonic Distance Sensor
  RHT1 = Humidity and Temperature Sensor RHT03
  Buzzer = Piezo Speaker
  R2 = Resistor [tolerance=±5% resistance=220 package="1206 [SMD]"]

nets:
  VCC: Argon1.3.3V, R1.P$1, HC-SR04_Sensor_1.VCC, RHT1.Vcc
  GND: Argon1.GND, HC-SR04_Sensor_1.GND, RHT1.GND_2, Buzzer.pin2, R2.Pin_1
  N1: Argon1.A1, R1.P$2, R2.Pin_0
  N2: Argon1.A3, RHT1.Data-signal
  N3: Argon1.A5, Buzzer.pin1
  N4: Argon1.D4, HC-SR04_Sensor_1.TRIG
  N5: Argon1.D5, HC-SR04_Sensor_1.ECHO

custom parts:
  Particle Argon: The Argon is a powerful Wi-Fi enabled development board that can act as either a standalone Wi-Fi endpoint or Wi-Fi enabled gateway for Particle Mesh networks. It is based on the Nordic nRF52840 and has built-in battery charging circuitry so it’s easy to connect a Li-Po and deploy your local network in minutes. The Argon is great for connecting existing projects to the Particle Device Cloud or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
